# Fritzing sketch Scheme (saved by Fritzing 0.9.4)
breadboards: 1

parts:
  SIM800L_BO1 = SIM800L BO
  U5 = NodeMCU V3.0
  U6 = LIPO-1000mAh [package=lipo-1000]

nets:
  N1: SIM800L_BO1.PIN2, U6.+
  N2: SIM800L_BO1.pin_4, U5.TX
  N3: SIM800L_BO1.pin_5, U5.RX
  N4: SIM800L_BO1.pin_6, U5.GND, U6.-

custom parts:
  NodeMCU V3.0: NodeMcu V3 Lua WIFI Development Board
